// Digital circuit Adder.dig as structural Verilog
module Adder (
  input  [7:0] a,
  input  [7:0] b,
  input  [1:0] funct,
  input  [3:0] flags,
  output [7:0] s,
  output c_out
);

  wire multiplexer_1_out, xor_1_out;
  wire [7:0] bitextender_1_out, xor_2_out;

  Multiplexer #(.Selector_Bits(2)) multiplexer_1 (
    .sel(funct), .in_0(1'b0), .in_1(1'b1), .in_2(1'b1), .in_3(1'b1), .out(multiplexer_1_out));
  xor xor_1 (xor_1_out, multiplexer_1_out, flags[2]);
  BitExtender #(.inputBits(1), .outputBits(8)) bitextender_1 (.in(flags[2]), .out(bitextender_1_out));
  assign xor_2_out = b ^ bitextender_1_out;  // XOr xor_2, 8 bits wide
  Add #(.Bits(8)) add_1 (.a(a), .b(xor_2_out), .c_i(xor_1_out), .s(s), .c_o(c_out));

  // Other names for the same wires on the sheet: Flag_V = flags[0]; Flag_Z = flags[1]; Flag_C = flags[2];
  //   Flag_N = flags[3]
endmodule
