// Digital circuit CPU.dig as structural Verilog
module CPU (
  input  [7:0] Data_IN,
  input  CLK,
  output [7:0] Data_OUT,
  output [15:0] Addr_OUT,
  output Mem_WE,
  output Mem_OE,
  output [3:0] opcode,
  output [15:0] pc,
  output [15:0] stack,
  output [7:0] uCode
);

  wire ALU_Out_Write_Data_Bus, ALU_Write_Flag_Register, and_1_out, Condition_Flag, Immediate_Write_Data_Bus,
       Instruction_ExFlag, IR0_Read_Data_Bus, IR1_Read_Data_Bus, IR2_Read_Data_Bus, multiplexer_1_out,
       nor_1_out, or_1_out, or_2_out, or_3_out, or_4_out, PCH_ovf, PCH_Read_Data_Bus, PCH_Write_Data_Bus,
       PCL_Read_Data_Bus, PCL_Write_Data_Bus, Program_Conter_Read_Address_Bus,
       Program_Conter_Write_Address_Bus, Program_Counter_Increase_Enable, RD_Read_Data_Bus,
       RD_write_Data_Bus, Read_Data_Bus, RS0_Write_Data_Bus, RS1_Write_Data_Bus, RS_Buffer,
       RS_plus_1_Write_Address_Bus, RS_Write_Address_Bus, SPH_ovf, SPH_Read_Data_Bus, SPH_Write_Data_Bus,
       SPL_Read_Data_Bus, SPL_Write_Data_Bus, Stack_Pointer_Decrease, Stack_Pointer_Increase,
       Stack_Pointer_Write_Address_Bus, uCode_Counter_Clear, uCode_Counter_Conditional_Clear,
       uCode_Counter_ovf, Write_Data_Bus, xor_1_out;
  wire [2:0] Instruction_Flag;
  wire [3:0] alu_1_p1, Instruction_Funct, Instruction_RS0, Instruction_RS1, multiplexer_2_out, register_1_q;
  wire [3:3] uCode_3_d;
  wire [4:1] uCode_3_d_2;
  wire [7:0] add_3_s, alu_1_p2, alu_1_p5, alu_1_p6, bitextender_2_out, driver_1_out, driver_2_out,
       driver_3_out, driver_5_out, driver_6_out, driver_21_out, driver_22_out, driver_23_out, driver_24_out;
  wire [7:4] Instruction_Immediate;
  wire [7:5] uCode_2_d;
  wire [15:0] add_1_s, add_2_s, bitextender_1_out, rs1_buf_q;

  or or_1 (or_1_out, and_1_out, uCode_Counter_Clear);
  and and_1 (and_1_out, uCode_Counter_Conditional_Clear, xor_1_out);
  xor xor_1 (xor_1_out, Instruction_ExFlag, Condition_Flag);
  Counter #(.Bits(4)) uCode_Counter (.en(1'b1), .C(CLK), .clr(or_1_out), .out(uCode[3:0]), .ovf(uCode_Counter_ovf));
  LED led_1 (.in(uCode_Counter_ovf));
  EEPROM #(.AddrBits(8), .Bits(8)) uCode_3 (
    .A({opcode, uCode[3:0]}), .CS(1'b1), .WE(1'b0), .OE(1'b1),
    .D({Mem_OE, Mem_WE, ALU_Write_Flag_Register, uCode_3_d_2, uCode_3_d[3]}));
  Decoder #(.Selector_Bits(4)) decoder_1 (
    .sel({uCode_3_d[3], uCode_2_d}), .out_1(PCL_Write_Data_Bus), .out_2(PCH_Write_Data_Bus),
    .out_3(SPL_Write_Data_Bus), .out_4(SPH_Write_Data_Bus), .out_5(RD_write_Data_Bus),
    .out_6(RS0_Write_Data_Bus), .out_7(RS1_Write_Data_Bus), .out_8(Immediate_Write_Data_Bus),
    .out_9(ALU_Out_Write_Data_Bus));  // open: out_0, out_10, out_11, out_12, out_13, out_14, out_15
  CounterPreset #(.Bits(8)) SPL (
    .en(SPH_ovf), .C(CLK), .dir(Stack_Pointer_Decrease), .in(driver_1_out), .ld(SPL_Read_Data_Bus),
    .clr(1'b0), .out(stack[15:8]));  // open: ovf
  or or_2 (or_2_out, PCL_Read_Data_Bus, Program_Conter_Read_Address_Bus);
  CounterPreset #(.Bits(8)) PCL (
    .en(Program_Counter_Increase_Enable), .C(PCH_ovf), .dir(1'b0), .in(driver_5_out), .ld(or_2_out),
    .clr(1'b0), .out(pc[15:8]));  // open: ovf
  EEPROM #(.AddrBits(8), .Bits(8)) uCode_2 (
    .A({opcode, uCode[3:0]}), .CS(1'b1), .WE(1'b0), .OE(1'b1),
    .D({uCode_2_d, RS_plus_1_Write_Address_Bus, RS_Write_Address_Bus, RS_Buffer, Stack_Pointer_Decrease, Stack_Pointer_Increase}));
  CounterPreset #(.Bits(8)) SPH (
    .en(or_3_out), .C(CLK), .dir(Stack_Pointer_Decrease), .in(driver_2_out), .ld(SPH_Read_Data_Bus),
    .clr(1'b0), .out(stack[7:0]), .ovf(SPH_ovf));
  assign driver_1_out = SPL_Read_Data_Bus ? driver_3_out : 8'bz;  // Driver driver_1
  assign driver_2_out = SPH_Read_Data_Bus ? driver_3_out : 8'bz;  // Driver driver_2
  or or_3 (or_3_out, Stack_Pointer_Increase, Stack_Pointer_Decrease);
  or or_4 (or_4_out, PCH_Read_Data_Bus, Program_Conter_Read_Address_Bus);
  EEPROM #(.AddrBits(8), .Bits(8)) uCode_1 (
    .A({opcode, uCode[3:0]}), .CS(1'b1), .WE(1'b0), .OE(1'b1),
    .D({Stack_Pointer_Write_Address_Bus, SPH_Read_Data_Bus, SPL_Read_Data_Bus, Write_Data_Bus, Read_Data_Bus, RD_Read_Data_Bus, PCH_Read_Data_Bus, PCL_Read_Data_Bus}));
  CounterPreset #(.Bits(8)) PCH (
    .en(Program_Counter_Increase_Enable), .C(CLK), .dir(1'b0), .in(driver_6_out), .ld(or_4_out), .clr(1'b0),
    .out(pc[7:0]), .ovf(PCH_ovf));
  assign driver_3_out = SPL_Write_Data_Bus ? stack[15:8] : 8'bz;  // Driver driver_3
  assign driver_3_out = SPH_Write_Data_Bus ? stack[7:0] : 8'bz;  // Driver driver_4
  assign driver_5_out = PCL_Read_Data_Bus ? driver_3_out : 8'bz;  // Driver driver_5
  assign driver_6_out = PCH_Read_Data_Bus ? driver_3_out : 8'bz;  // Driver driver_6
  assign driver_3_out = PCH_Write_Data_Bus ? pc[7:0] : 8'bz;  // Driver driver_7
  EEPROM #(.AddrBits(8), .Bits(8)) uCode_0 (
    .A({opcode, uCode[3:0]}), .CS(1'b1), .WE(1'b0), .OE(1'b1),
    .D({IR2_Read_Data_Bus, IR1_Read_Data_Bus, IR0_Read_Data_Bus, Program_Conter_Read_Address_Bus, Program_Conter_Write_Address_Bus, Program_Counter_Increase_Enable, uCode_Counter_Clear, uCode_Counter_Conditional_Clear}));
  assign Addr_OUT = Stack_Pointer_Write_Address_Bus ? stack : 16'bz;  // Driver driver_8
  assign {driver_5_out, driver_6_out} = Program_Conter_Read_Address_Bus ? Addr_OUT : 16'bz;  // Driver driver_9
  assign driver_3_out = PCL_Write_Data_Bus ? pc[15:8] : 8'bz;  // Driver driver_10
  assign Addr_OUT = Program_Conter_Write_Address_Bus ? pc : 16'bz;  // Driver driver_11
  assign driver_3_out = Read_Data_Bus ? Data_IN : 8'bz;  // Driver driver_12
  assign Data_OUT = Write_Data_Bus ? driver_3_out : 8'bz;  // Driver driver_13
  assign Addr_OUT = RS_Write_Address_Bus ? add_1_s : 16'bz;  // Driver driver_14
  assign Addr_OUT = RS_plus_1_Write_Address_Bus ? add_2_s : 16'bz;  // Driver driver_15
  assign driver_3_out = ALU_Out_Write_Data_Bus ? add_3_s : 8'bz;  // Driver driver_16
  assign driver_3_out = RD_write_Data_Bus ? alu_1_p5 : 8'bz;  // Driver driver_17
  assign driver_3_out = RS1_Write_Data_Bus ? alu_1_p5 : 8'bz;  // Driver driver_18
  assign driver_3_out = RS0_Write_Data_Bus ? alu_1_p6 : 8'bz;  // Driver driver_19
  nor nor_1 (nor_1_out, Instruction_Flag[0], Instruction_Flag[1], Instruction_Flag[2], Instruction_ExFlag);
  Add #(.Bits(16)) add_1 (.a(bitextender_1_out), .b(rs1_buf_q), .c_i(1'b0), .s(add_1_s));  // open: c_o
  Add #(.Bits(16)) add_2 (.a(16'h1), .b(add_1_s), .c_i(1'b0), .s(add_2_s));  // open: c_o
  Add #(.Bits(8)) add_3 (.a(alu_1_p2), .b(bitextender_2_out), .c_i(1'b1), .s(add_3_s));  // open: c_o
  Multiplexer multiplexer_1 (.sel(nor_1_out), .in_0(RD_Read_Data_Bus), .in_1(1'b0), .out(multiplexer_1_out));
  BitExtender bitextender_1 (.in({Instruction_Immediate, Instruction_Funct}), .out(bitextender_1_out));
  Register #(.Bits(4)) register_1 (.D(alu_1_p1), .C(CLK), .en(ALU_Write_Flag_Register), .Q(register_1_q));
  assign driver_3_out = Immediate_Write_Data_Bus ? {Instruction_Immediate, Instruction_Funct} : 8'bz;  // Driver driver_20
  Register #(.Bits(8)) IR_2 (
    .D(driver_21_out), .C(CLK), .en(IR2_Read_Data_Bus), .Q({Instruction_Immediate, Instruction_Funct}));
  assign driver_21_out = IR2_Read_Data_Bus ? driver_3_out : 8'bz;  // Driver driver_21
  Multiplexer #(.Bits(4)) multiplexer_2 (
    .sel(RD_write_Data_Bus), .in_0(Instruction_RS1), .in_1({Instruction_ExFlag, Instruction_Flag}),
    .out(multiplexer_2_out));
  Register #(.Bits(8)) rs0_buf (.D(alu_1_p6), .C(CLK), .en(RS_Buffer), .Q(rs1_buf_q[15:8]));
  Register #(.Bits(8)) rs1_buf (.D(alu_1_p5), .C(CLK), .en(RS_Buffer), .Q(rs1_buf_q[7:0]));
  BitExtender #(.inputBits(4), .outputBits(8)) bitextender_2 (.in(Instruction_Immediate), .out(bitextender_2_out));
  // ALU alu_1: pin names not known; wires that end beside it: alu_1_p1, alu_1_p2, Instruction_Funct, register_1_q, alu_1_p5, alu_1_p6
  ConditionFlags conditionflags_1 (
    .v(register_1_q[0]), .z(register_1_q[1]), .c(register_1_q[2]), .n(register_1_q[3]),
    .flag(Instruction_Flag), .f(Condition_Flag));
  Register #(.Bits(8)) IR_1 (
    .D(driver_22_out), .C(CLK), .en(IR1_Read_Data_Bus), .Q({Instruction_RS1, Instruction_RS0}));
  assign driver_22_out = IR1_Read_Data_Bus ? driver_3_out : 8'bz;  // Driver driver_22
  assign driver_23_out = RD_Read_Data_Bus ? driver_3_out : 8'bz;  // Driver driver_23
  RegisterFile #(.AddrBits(4), .Bits(8)) Register_File (
    .Din(driver_23_out), .we(multiplexer_1_out), .Rw({Instruction_ExFlag, Instruction_Flag}), .C(CLK),
    .Ra(Instruction_RS0), .Rb(multiplexer_2_out), .Da(alu_1_p6), .Db(alu_1_p5));
  Register #(.Bits(8)) IR_0 (
    .D(driver_24_out), .C(CLK), .en(IR0_Read_Data_Bus), .Q({Instruction_ExFlag, Instruction_Flag, opcode}));
  assign driver_24_out = IR0_Read_Data_Bus ? driver_3_out : 8'bz;  // Driver driver_24

  assign uCode[7:4] = opcode;

  // Other names for the same wires on the sheet: Instruction_Opcode[3:0] = opcode;
  //   Instruction_RD[3:0] = {Instruction_ExFlag, Instruction_Flag}; Memory_Write_Enable = Mem_WE;
  //   Memory_Output_Enable = Mem_OE; Clock = CLK; Instruction_Immediate[3:0] = Instruction_Funct

  // Notes on the sheet:
  //   uCode
  //   Stack Pointer
  //   Program Counter
  //   contents of uCode_3 (hex, n*v repeats v):
  //   80,80,80,13*0,80,80,80,13*0,80,80,80,1,12*0,80,80,80,0,80,11*0
  //   ,80,80,80,0,40,11*0,80,80,80,21,12*0,80,80,80,13*0,80,80,80,40
  //   ,12*0,4*80,12*0,80,80,80,45*0,80,80,80,40,40,11*0,5*80,11*0,80,80,80
  //   ,0,40,40
  //   contents of uCode_2 (hex, n*v repeats v):
  //   19*0,c0,31*0,c,8,14*0,c,a8,14*0,20,15*0,c,8,13*0,1,a0,15*0,2,15*0
  //   ,c0,e0,45*0,1,21,40,14*0,2,2,14*0,1,21,40,c0,e0
  //   contents of uCode_1 (hex, n*v repeats v):
  //   8,8,8,13*0,8,8,8,4,12*0,8,8,8,4,12*0,8,8,8,0,c,11*0,8,8,8,0,10
  //   ,11*0,8,8,8,4,12*0,8,8,8,13*0,8,8,8,90,12*0,8,8,8,8c,12*0,8,8,8
  //   ,20,40,43*0,8,8,8,90,90,11*0,8,8,8,8a,89,11*0,8,8,8,0,90,90,1,2
  //   contents of uCode_0 (hex, n*v repeats v):
  //   2c,4c,8c,13*0,2c,4c,8c,2,12*0,2c,4c,8c,2,12*0,2c,4c,8c,0,2,11*0
  //   ,2c,4c,8c,0,2,11*0,2c,4c,8c,2,12*0,2c,4c,8c,1,12,11*0,2c,4c,8c
  //   ,2,12*0,2c,4c,8c,2,12*0,2c,4c,8c,0,2,43*0,2c,4c,8c,0,2,11*0,2c
  //   ,4c,8c,0,2,11*0,2c,4c,8c,4*0,2
  //   Register File
  //   Address Calculation
  //   ALU
  //   Status Register
  //   Instruction Register
endmodule
