// Digital circuit Clock.dig as structural Verilog
module Clock (
  input  CLK,
  input  MODE,
  input  STEP,
  output SIGNAL
);

  wire and_1_out, and_2_out, not_1_out;

  not not_1 (not_1_out, MODE);
  and and_1 (and_1_out, MODE, STEP);
  and and_2 (and_2_out, CLK, not_1_out);
  or or_1 (SIGNAL, and_2_out, and_1_out);
endmodule
