// Digital circuit ConditionFlags.dig as structural Verilog
module ConditionFlags (
  input  v,
  input  z,
  input  c,
  input  n,
  input  [2:0] flag,
  output f
);

  wire nc, nz, or_1_out, or_2_out, xor_1_out;

  not not_1 (nz, z);
  not not_2 (nc, c);
  xor xor_1 (xor_1_out, n, v);
  or or_1 (or_1_out, z, xor_1_out);
  or or_2 (or_2_out, nc, z);
  Multiplexer #(.Selector_Bits(3)) multiplexer_1 (
    .sel(flag), .in_0(z), .in_1(nz), .in_2(nc), .in_3(c), .in_4(or_2_out), .in_5(or_1_out), .in_6(xor_1_out),
    .in_7(1'b1), .out(f));
endmodule
