// Digital circuit FlagGeneration.dig as structural Verilog
module FlagGeneration (
  input  [7:0] s,
  input  [7:0] a,
  input  [7:0] b,
  input  c_in,
  input  c_out,
  output n,
  output z,
  output v
);

  wire [7:0] not_1_out;

  assign not_1_out = ~s;  // Not not_1, 8 bits wide
  and and_1 (z, not_1_out[7], not_1_out[6], not_1_out[5], not_1_out[4], not_1_out[3], not_1_out[2], not_1_out[1], not_1_out[0]);
  PullDown pulldown_1 (.out(c_out));
  OverflowFlag overflowflag_1 (.a_msb(a[7]), .b_msb(b[7]), .s_msb(s[7]), .c_in(c_in), .c_out(c_out), .of(v));

  assign n = s[7];
endmodule
