// Digital circuit OverflowFlag.dig as structural Verilog
module OverflowFlag (
  input  a_msb,
  input  b_msb,
  input  s_msb,
  input  c_in,
  input  c_out,
  output of
);

  wire and_1_out, and_2_out, not_1_out, not_2_out, not_3_out, not_4_out, not_5_out;

  not not_1 (not_1_out, a_msb);
  not not_2 (not_2_out, b_msb);
  not not_3 (not_3_out, s_msb);
  not not_4 (not_4_out, c_in);
  not not_5 (not_5_out, c_out);
  and and_1 (and_1_out, not_1_out, not_2_out, s_msb, not_4_out, c_out);
  and and_2 (and_2_out, a_msb, b_msb, not_3_out, c_in, not_5_out);
  or or_1 (of, and_1_out, and_2_out);
endmodule
