// Digital circuit Puter.dig as structural Verilog
module Puter (
  input  M,
  input  CLK
);

  wire CLK_t, demultiplexer_3_out_1, demultiplexer_3_out_2, demultiplexer_4_out_1, demultiplexer_4_out_2,
       IO_OE, IO_WE, Kb_H, Kb_L, MEM_OE, MEM_WE, RAM_OE, RAM_WE, ROM_OE, S_out, T_erm_WE, undriven,
       undriven_2, undriven_3, undriven_4;
  wire [1:0] MEM_SEL;
  wire [7:0] Data_In, Data_Out, pulldown_1_out;
  wire [13:0] MEM_ADDR;
  wire [15:0] keyboard_1_d;

  Clock clock_1 (.CLK(CLK), .MODE(M), .STEP(S_out), .SIGNAL(CLK_t));
  Button S (.out(S_out));
  Demultiplexer #(.Selector_Bits(4)) demultiplexer_1 (
    .sel(MEM_ADDR[11:8]), .in(IO_WE), .out_2(T_erm_WE));  // open: out_0, out_1, out_3, out_4, out_5, out_6, out_7, out_8, out_9, out_10, out_11, out_12, out_13, out_14, out_15
  PullDown #(.Bits(8)) pulldown_1 (.out(pulldown_1_out));
  Terminal terminal_1 (.D(pulldown_1_out), .C(CLK_t), .en(1'b1));
  assign pulldown_1_out = T_erm_WE ? Data_Out : 8'bz;  // Driver driver_1
  Keyboard keyboard_1 (.C(CLK_t), .en(1'b1), .D(keyboard_1_d));  // open: av
  // Probe on {MEM_SEL, MEM_ADDR}
  Demultiplexer #(.Selector_Bits(4)) demultiplexer_2 (
    .sel(MEM_ADDR[11:8]), .in(IO_OE), .out_0(Kb_L), .out_1(Kb_H));  // open: out_2, out_3, out_4, out_5, out_6, out_7, out_8, out_9, out_10, out_11, out_12, out_13, out_14, out_15
  CPU cpu_1 ();
  assign Data_In = Kb_L ? keyboard_1_d[7:0] : 8'bz;  // Driver driver_2
  assign Data_In = Kb_H ? keyboard_1_d[15:8] : 8'bz;  // Driver driver_3
  EEPROM #(.AddrBits(14), .Bits(8)) eeprom_1 (.A(MEM_ADDR), .CS(1'b1), .WE(1'b0), .OE(ROM_OE), .D(Data_In));
  // Probe on undriven
  // Probe on undriven_2
  // Probe on undriven_3
  // Probe on undriven_4
  RAMDualPort #(.AddrBits(14), .Bits(8)) ramdualport_1 (
    .A(MEM_ADDR), .Din(Data_Out), .str(RAM_WE), .C(CLK_t), .ld(RAM_OE), .D(Data_In));
  or or_1 (RAM_WE, demultiplexer_3_out_1, demultiplexer_3_out_2);
  or or_2 (RAM_OE, demultiplexer_4_out_1, demultiplexer_4_out_2);
  Demultiplexer #(.Selector_Bits(2)) demultiplexer_3 (
    .sel(MEM_SEL), .in(MEM_WE), .out_1(demultiplexer_3_out_1), .out_2(demultiplexer_3_out_2), .out_3(IO_WE));  // open: out_0
  Demultiplexer #(.Selector_Bits(2)) demultiplexer_4 (
    .sel(MEM_SEL), .in(MEM_OE), .out_0(ROM_OE), .out_1(demultiplexer_4_out_1), .out_2(demultiplexer_4_out_2),
    .out_3(IO_OE));

  // Notes on the sheet:
  //   M: default 1
  //   CLK: Hz: 500
  //   Clock
  //   IO Select
  //   Terminal
  //   Keyboard
  //   CPU
  //   contents of eeprom_1 (hex, n*v repeats v):
  //   72,0,3f,82,0,ff,9,87,0,d2,0,10,e2,0,0,72,0,0,82,0,18,e,87,0,92
  //   ,0,c2,a2,0,0,b2,0,40,c2,0,0,13,ed,0,5,1,2,72,0,0,82,0,4b,86,87
  //   ,0,14,a9,0,14,cb,0,22,0,1,d5,2d,0,e5,e,1,72,0,0,82,0,24,f6,87
  //   ,0,d,4020*0,48,65,6c,6c,6f,20,57,6f,72,6c,64,21,20,4a,75,73,74
  //   ,20,61,20,74,65,73,74,20,6d,65,73,73,61,67,65,2e
  //   ROM
  //   Device signals
  //   RAM
endmodule
